# Fritzing sketch PiIntro (saved by Fritzing 0.9.0b)
breadboards: 1

parts:
  Raspberry_Pi1 = Raspberry Pi (Model B)
  S1 = Pushbutton [package="[THT]"]
  LED1 = LED - 5mm [color="Red (633nm)" package="5 mm [THT]"]
  R1 = Resistor [tolerance=±5% resistance=220 package=THT]

nets:
  N1: Raspberry_Pi1.GND, S1.Pin_1, S1.Pin_2, LED1.cathode
  N2: Raspberry_Pi1.#18, S1.Pin_3, S1.Pin_4
  N3: Raspberry_Pi1.#25, LED1.anode, R1.Pin_0, R1.Pin_1

custom parts:
  Raspberry Pi (Model B): Raspberry Pi Single-board Computer, Model B
